# Fritzing sketch wiringchart (saved by Fritzing 0.9.3b)
breadboards: 1

parts:
  IC1 = L293D [package=THT]
  M1 = DC Motor
  M2 = DC Motor
  BAT1 = BC9VPC [package=bc9vpc]
  JP1 = Header 2 [package=jst-2-smd-vert]
  U1 = ENCODER_2LED [package=encoder_led_2]
  J3 = Basic Servo
  J4 = Basic Servo
  MCU1 = Raspberry Pi B+  # not connected
  MCU1_2 = Raspberry Pi B+
  U2 = ENCODER_2LED [package=encoder_led_2]

nets:
  N1: IC1.In_1, MCU1_2.GPIO11
  N2: IC1.Out_1_(_Controlled_by_Enable_1_), M2.pin_1
  GND: IC1.0V, BAT1.V-, JP1.1, U1.-, J3.gnd, J4.gnd, MCU1_2.GND, U2.-
  N3: IC1.Out_2_(_Controlled_by_Enable_1_), M2.pin_2
  N4: IC1.+Vmotor, BAT1.V+, JP1.2
  N5: IC1.Out_3_(_Controlled_by_Enable_2_), M1.pin_2
  N6: IC1.Out_4_(_Controlled_by_Enable_2_), M1.pin_1
  N7: U1.B, MCU1_2.GPIO27
  N8: U1.C, MCU1_2.GPIO17
  3V3: U1.SW, MCU1_2.3v3, MCU1_2.3V3, U2.SW
  VCC: J3.vcc, J4.vcc
  N9: J3.pulse, MCU1_2.GPIO12
  N10: MCU1_2.GPIO20, U2.B
  N11: MCU1_2.GPIO16, U2.C

notes:
  The Pi Bot breadboards have only 17 columns; ignore the last 3 in this image
  For the DC motors, green is negative and yellow is positive
  BEC
  Claw
  Arm

// code stored in the sketch: Untitled.ino

